// Logisim project add1bitr.circ as structural Verilog: 2 circuits, main circuit main
module main (
  input  in_1,
  output out_2
);

  // NOT_Gate not_1 is placed but not wired
  // AND_Gate and_1 is placed but not wired
endmodule

module add1Bit (
  input  A,
  input  B,
  input  C_in,
  output Z,
  output C_OUT
);

  wire and_1_out, and_2_out, and_3_out, xor_1_out;

  xor xor_1 (xor_1_out, A, B);
  and and_1 (and_1_out, A, B);
  and and_2 (and_2_out, A, C_in);
  and and_3 (and_3_out, B, C_in);
  xor xor_2 (Z, xor_1_out, C_in);
  or or_1 (C_OUT, and_1_out, and_2_out, and_3_out);
endmodule
